// Logisim project s-mips.circ as structural Verilog: 14 circuits, main circuit S-MIPS Board
module S_MIPS_Board (
  input  DESHABILITAR_DISPATCHER,
  output halt
);

  wire button_1_out, CLK, CS, d_ff_1_q, LCLR, LoadRAM, LoadRAMOn, LW, R_R_W, R_W, ram_dispatcher_1_finished,
       RCS, Reset_out, RST, TTY_EN;
  wire [2:0] KDB;
  wire [3:0] LMask, Mask, ram_1_read_time, ram_1_write_time, RMask;
  wire [6:0] KDB_DATA, TTY_DATA;
  wire [15:0] Addr, LAddr, RAddr;
  wire [31:0] I0, I1, I2, I3, LData, ram_1_data_out_0, ram_1_data_out_1, ram_1_data_out_2, ram_1_data_out_3,
       RI0, RI1, RI2, RI3;

  TTY #(.rows(25), .cols(80)) tty_1 (.data(TTY_DATA), .clk(CLK), .we(TTY_EN), .clr(RST));
  not not_1 (LoadRAMOn, ram_dispatcher_1_finished);
  RAM_Dispatcher ram_dispatcher_1 (
    .WriteTime(ram_1_write_time), .Clock(CLK), .Data(LData), .Address(LAddr), .Mask(LMask),
    .Finished(ram_dispatcher_1_finished), .Write(LW), .CLR(LCLR));
  Keyboard #(.buflen(64)) keyboard_1 (.clk(CLK), .re(KDB[0]), .avail(KDB[2]), .data(KDB_DATA));  // open: clr
  RAM ram_1 (
    .Address(RAddr), .Data_Out_0(ram_1_data_out_0), .Data_Out_1(ram_1_data_out_1),
    .Data_Out_2(ram_1_data_out_2), .Data_Out_3(ram_1_data_out_3), .Data_In_0(RI0), .Data_In_1(RI1),
    .Data_In_2(RI2), .Data_In_3(RI3), .Mask(RMask), .nRead_Write(R_R_W), .Chip_Select(RCS),
    .Read_Time(ram_1_read_time), .Reset(button_1_out), .Write_Time(ram_1_write_time));
  Button button_1 (.out(button_1_out));
  D_Flip_Flop d_ff_1 (.clk(CLK), .D(1'b1), .Q(d_ff_1_q), .reset(Reset_out));  // open: Qn, preset, en
  Button Reset (.out(Reset_out));
  S_MIPS s_mips_1 (
    .Kbd_Enable(KDB[0]), .Address(Addr), .Kbd_Clear(KDB[1]), .Kbd_Available(KDB[2]), .RAM_In_0(I0),
    .Kbd_ASCII_Data(KDB_DATA), .RAM_In_1(I1), .TTY_Enable(TTY_EN), .RAM_In_2(I2), .RAM_In_3(I3),
    .TTY_ASCII_Data(TTY_DATA), .Reset(RST), .RAM_Out_0(ram_1_data_out_0), .Clock(CLK),
    .RAM_Out_1(ram_1_data_out_1), .Stop(halt), .RAM_Out_2(ram_1_data_out_2), .RAM_Out_3(ram_1_data_out_3),
    .Mask(Mask), .Read_Time(ram_1_read_time), .Write_Time(ram_1_write_time), .nRead_Write(R_W),
    .Chip_Select(CS));
  D_Flip_Flop d_ff_2 (.clk(CLK), .D(d_ff_1_q), .Qn(LCLR), .reset(Reset_out));  // open: Q, preset, en
  or or_1 (RST, LCLR, LoadRAM);
  Clock clock_1 (.out(CLK));
  Multiplexer #(.width(32), .enable("false")) multiplexer_1 (.in0(I0), .in1(LData), .out(RI0), .sel(LoadRAM));
  Multiplexer #(.width(32), .enable("false")) multiplexer_2 (.in0(I1), .in1(LData), .out(RI1), .sel(LoadRAM));
  Multiplexer #(.width(32), .enable("false")) multiplexer_3 (.in0(I2), .in1(LData), .out(RI2), .sel(LoadRAM));
  Multiplexer #(.width(32), .enable("false")) multiplexer_4 (.in0(I3), .in1(LData), .out(RI3), .sel(LoadRAM));
  and and_1 (LoadRAM, ~DESHABILITAR_DISPATCHER, LoadRAMOn);  // AND_Gate
  Multiplexer #(.width(16), .enable("false")) multiplexer_5 (.in0(Addr), .in1(LAddr), .out(RAddr), .sel(LoadRAM));
  Multiplexer #(.width(4), .enable("false")) multiplexer_6 (.in0(Mask), .in1(LMask), .out(RMask), .sel(LoadRAM));
  Multiplexer #(.enable("false")) multiplexer_7 (.in0(CS), .in1(LW), .out(RCS), .sel(LoadRAM));
  Multiplexer #(.enable("false")) multiplexer_8 (.in0(R_W), .in1(LW), .out(R_R_W), .sel(LoadRAM));

  // Notes on the sheet:
  //   NO MODIFICAR
  //   Keyboard
endmodule

module S_MIPS (
  input  Kbd_Available,
  input  [6:0] Kbd_ASCII_Data,
  input  [31:0] RAM_Out_0,
  input  [31:0] RAM_Out_1,
  input  Reset,
  input  [31:0] RAM_Out_2,
  input  Clock,
  input  [31:0] RAM_Out_3,
  input  [3:0] Read_Time,
  input  [3:0] Write_Time,
  output Kbd_Enable,
  output [15:0] Address,
  output Kbd_Clear,
  output TTY_Enable,
  output [6:0] TTY_ASCII_Data,
  output Stop,
  output [31:0] RAM_In_0,
  output [31:0] RAM_In_1,
  output [31:0] RAM_In_2,
  output [31:0] RAM_In_3,
  output [3:0] Mask,
  output nRead_Write,
  output Chip_Select
);


  // Other names for the same wires on the sheet: CLK = Clock; CLR = Reset; CS = Chip_Select;
  //   KBD_AVAIL = Kbd_Available; KBD_CLR = Kbd_Clear; KBD_DATA[6:0] = Kbd_ASCII_Data; RAM_A[15:0] = Address;
  //   RAM_INPUT_0[31:0] = RAM_In_0; RAM_INPUT_1[31:0] = RAM_In_1; RAM_INPUT_2[31:0] = RAM_In_2;
  //   RAM_INPUT_3[31:0] = RAM_In_3; RAM_MASK[3:0] = Mask; RAM_OUTPUT_0[31:0] = RAM_Out_0;
  //   RAM_OUTPUT_1[31:0] = RAM_Out_1; RAM_OUTPUT_2[31:0] = RAM_Out_2; RAM_OUTPUT_3[31:0] = RAM_Out_3;
  //   RW = nRead_Write; TTY_DATA[6:0] = TTY_ASCII_Data

  // Notes on the sheet:
  //   RAM ADDRESS
  //   DATA FROM RAM
  //   DATA TO RAM
  //   DATA WRITE MASK
  //   RAM TIMING
  //   RAM CONTROL
  //   KEYBOARD
  //   TTY
  //   SEQUENCING
endmodule

module RAM (
  input  [15:0] Address,
  input  [31:0] Data_In_0,
  input  [31:0] Data_In_1,
  input  [31:0] Data_In_2,
  input  [31:0] Data_In_3,
  input  [3:0] Mask,
  input  nRead_Write,
  input  Chip_Select,
  input  Reset,
  output [31:0] Data_Out_0,
  output [31:0] Data_Out_1,
  output [31:0] Data_Out_2,
  output [31:0] Data_Out_3,
  output [3:0] Read_Time,
  output [3:0] Write_Time
);

  wire and_2_out, and_3_out, and_4_out, and_5_out, and_6_out, and_7_out, and_8_out, and_9_out, Changed, CLK,
       comparator_2_eq, comparator_3_eq, comparator_4_eq, comparator_5_eq, comparator_6_eq, Count,
       demultiplexer_3_out0, Idle, Idle_q, Load, Load0, Load1, nand_1_out, or_1_out, or_2_out, or_3_out,
       or_4_out, or_5_out, or_6_out, or_7_out, or_8_out, or_9_out, or_10_out, Proc_q, Update_Mem, Zero_Time;
  wire [3:0] counter_1_q, multiplexer_1_out, subtractor_1_out;
  wire [31:0] register_1_q, register_2_q, register_3_q, register_4_q, register_5_q;

  // Probe on 4'b0011
  // Probe on 4'b0010
  Multiplexer #(.width(4), .enable("false")) multiplexer_1 (
    .in0(4'b0011), .in1(4'b0010), .out(multiplexer_1_out), .sel(nRead_Write));
  or or_1 (or_1_out, Idle, Update_Mem);
  or or_2 (or_2_out, ~Chip_Select, Reset);  // OR_Gate
  Subtractor #(.width(4)) subtractor_1 (.a(multiplexer_1_out), .b(4'b0010), .out(subtractor_1_out));  // open: bin, bout
  D_Flip_Flop u_Idle (.clk(CLK), .D(or_1_out), .Q(Idle_q), .preset(or_2_out));  // open: Qn, en, reset
  Demultiplexer #(.enable("false")) demultiplexer_1 (.out0(Idle), .out1(Load0), .in(Idle_q), .sel(Changed));
  // Probe on counter_1_q
  Counter #(.width(4), .max('hf)) counter_1 (
    .load(Load), .D(subtractor_1_out), .count(Count), .Q(counter_1_q), .clk(CLK), .clr(or_3_out));  // open: carry
  or or_3 (or_3_out, ~Chip_Select, Reset);  // OR_Gate
  Comparator #(.width(4), .mode("unsigned")) comparator_1 (
    .a(4'b0000), .b(counter_1_q), .eq(Zero_Time));  // open: gt, lt
  or or_4 (or_4_out, Count, Load0, Load1);
  Register #(.width(32)) register_1 (.D(Data_In_0), .en(Chip_Select), .Q(register_1_q), .clk(CLK), .clr(or_5_out));
  or or_5 (or_5_out, ~Chip_Select, Reset);  // OR_Gate
  Register #(.width(32)) register_2 (.D(Data_In_1), .en(Chip_Select), .Q(register_2_q), .clk(CLK), .clr(or_6_out));
  or or_6 (or_6_out, ~Chip_Select, Reset);  // OR_Gate
  Register #(.width(32)) register_3 (.D(Data_In_2), .en(Chip_Select), .Q(register_3_q), .clk(CLK), .clr(or_7_out));
  or or_7 (or_7_out, ~Chip_Select, Reset);  // OR_Gate
  Register #(.width(32)) register_4 (.D(Data_In_3), .en(Chip_Select), .Q(register_4_q), .clk(CLK), .clr(or_8_out));
  or or_8 (or_8_out, ~Chip_Select, Reset);  // OR_Gate
  Register #(.width(32)) register_5 (
    .D({{11{1'b1}}, nRead_Write, Mask, Address}), .en(Chip_Select), .Q(register_5_q), .clk(CLK),
    .clr(or_9_out));
  or or_9 (or_9_out, ~Chip_Select, Reset);  // OR_Gate
  D_Flip_Flop Proc (.clk(CLK), .D(or_4_out), .Q(Proc_q), .reset(or_10_out));  // open: Qn, preset, en
  or or_10 (or_10_out, ~Chip_Select, Reset);  // OR_Gate
  Demultiplexer #(.enable("false")) demultiplexer_2 (
    .out0(Count), .out1(Update_Mem), .in(demultiplexer_3_out0), .sel(Zero_Time));
  Demultiplexer #(.enable("false")) demultiplexer_3 (
    .out0(demultiplexer_3_out0), .out1(Load1), .in(Proc_q), .sel(Changed));
  Clock clock_1 (.out(CLK));
  Comparator #(.width(32)) comparator_2 (.a(register_1_q), .b(Data_In_0), .eq(comparator_2_eq));  // open: gt, lt
  Comparator #(.width(32)) comparator_3 (.a(register_2_q), .b(Data_In_1), .eq(comparator_3_eq));  // open: gt, lt
  Comparator #(.width(32)) comparator_4 (.a(register_3_q), .b(Data_In_2), .eq(comparator_4_eq));  // open: gt, lt
  Comparator #(.width(32)) comparator_5 (.a(register_4_q), .b(Data_In_3), .eq(comparator_5_eq));  // open: gt, lt
  Comparator #(.width(32)) comparator_6 (
    .a(register_5_q), .b({{11{1'b1}}, nRead_Write, Mask, Address}), .eq(comparator_6_eq));  // open: gt, lt
  nand nand_1 (nand_1_out, comparator_6_eq, comparator_2_eq, comparator_3_eq, comparator_4_eq, comparator_5_eq);
  and and_1 (Changed, nand_1_out, Chip_Select);
  or or_11 (Load, Count, Load1, Load0);
  and and_2 (and_2_out, Mask[0], Update_Mem, nRead_Write);
  and and_3 (and_3_out, Mask[1], Update_Mem, nRead_Write);
  and and_4 (and_4_out, Mask[2], Update_Mem, nRead_Write);
  and and_5 (and_5_out, Mask[3], Update_Mem, nRead_Write);
  RAM_part #(.addrWidth(16), .dataWidth(32), .bus("separate")) ram_1 (
    .addr(Address), .din(Data_In_0), .data(Data_Out_0), .str(and_2_out), .sel(Chip_Select), .clk(CLK),
    .ld(and_6_out), .clr(Reset));
  and and_6 (and_6_out, ~nRead_Write, Idle);  // AND_Gate
  RAM_part #(.addrWidth(16), .dataWidth(32), .bus("separate")) ram_2 (
    .addr(Address), .din(Data_In_1), .data(Data_Out_1), .str(and_3_out), .sel(Chip_Select), .clk(CLK),
    .ld(and_7_out), .clr(Reset));
  and and_7 (and_7_out, ~nRead_Write, Idle);  // AND_Gate
  RAM_part #(.addrWidth(16), .dataWidth(32), .bus("separate")) ram_3 (
    .addr(Address), .din(Data_In_2), .data(Data_Out_2), .str(and_4_out), .sel(Chip_Select), .clk(CLK),
    .ld(and_8_out), .clr(Reset));
  and and_8 (and_8_out, ~nRead_Write, Idle);  // AND_Gate
  RAM_part #(.addrWidth(16), .dataWidth(32), .bus("separate")) ram_4 (
    .addr(Address), .din(Data_In_3), .data(Data_Out_3), .str(and_5_out), .sel(Chip_Select), .clk(CLK),
    .ld(and_9_out), .clr(Reset));
  and and_9 (and_9_out, ~nRead_Write, Idle);  // AND_Gate

  assign Read_Time = 4'b0011;
  assign Write_Time = 4'b0010;

  // Other names for the same wires on the sheet: M0 = Mask[0]; M1 = Mask[1]; M2 = Mask[2]; M3 = Mask[3];
  //   RW = nRead_Write; CLR = Reset; CS = Chip_Select; Load2 = Count

  // Notes on the sheet:
  //   NO MODIFICAR
  //   excepto quizás los valores RT y WT
  //   BANK0
  //   BANK1
  //   BANK2
  //   BANK3
endmodule

module RAM_Dispatcher (
  input  [3:0] WriteTime,
  input  Clock,
  input  CLR,
  output [31:0] Data,
  output [15:0] Address,
  output [3:0] Mask,
  output Finished,
  output Write
);

  wire demultiplexer_2_out1, demultiplexer_3_out1, End, IDLE_q, IncAddr, Load, or_1_out, or_2_out, While_q,
       WriteEnd;
  wire [3:0] counter_1_q;
  wire [31:0] CurrentAddress_q;

  Counter #(.width(32), .max('hffffffff)) CurrentAddress (
    .count(IncAddr), .Q({CurrentAddress_q[31:18], Address, CurrentAddress_q[1:0]}), .clk(Clock), .clr(CLR));  // open: load, D, carry
  or or_1 (or_1_out, IncAddr, demultiplexer_3_out1, Finished);
  D_Flip_Flop IDLE (.clk(Clock), .D(or_1_out), .Q(IDLE_q), .preset(CLR));  // open: Qn, en, reset
  Demultiplexer #(.enable("false")) demultiplexer_1 (.out0(Load), .out1(Finished), .in(IDLE_q), .sel(End));
  D_Flip_Flop While (.clk(Clock), .D(or_2_out), .Q(While_q), .reset(CLR));  // open: Qn, preset, en
  or or_2 (or_2_out, Write, Load);
  RAM_part #(.addrWidth(18), .dataWidth(32)) ram_1 (
    .addr({Address, CurrentAddress_q[1:0]}), .data(Data), .clk(Clock));  // open: sel, ld, clr
  Demultiplexer #(.enable("false")) demultiplexer_2 (
    .out0(Write), .out1(demultiplexer_2_out1), .in(While_q), .sel(WriteEnd));
  Decoder #(.select(2)) decoder_1 (
    .out0(Mask[0]), .out1(Mask[1]), .out2(Mask[2]), .out3(Mask[3]), .sel(CurrentAddress_q[1:0]));  // open: en
  Demultiplexer #(.enable("false")) demultiplexer_3 (
    .out0(IncAddr), .out1(demultiplexer_3_out1), .in(demultiplexer_2_out1), .sel(End));
  Counter #(.width(4), .max('hf)) counter_1 (
    .load(Load), .D(WriteTime), .count(Write), .Q(counter_1_q), .clk(Clock));  // open: carry, clr
  Comparator #(.width(32)) comparator_1 (.a(Data), .b({32{1'b1}}), .eq(End));  // open: gt, lt
  Comparator #(.width(4)) comparator_2 (.a(4'b0000), .b(counter_1_q), .eq(WriteEnd));  // open: gt, lt

  // Other names for the same wires on the sheet: CLK = Clock; Count = Write; WT[3:0] = WriteTime
endmodule

module Register_File (
  input  [4:0] in_1,
  input  [31:0] in_2,
  input  [4:0] in_3,
  input  [4:0] in_4,
  input  [31:0] in_5,
  input  in_6,
  input  in_7,
  input  in_8,
  input  [31:0] in_9,
  input  in_10,
  output [31:0] R1,
  output [31:0] HI_Out,
  output [31:0] R2,
  output [31:0] LO_Out
);

  wire decoder_1_out0, decoder_1_out1, decoder_1_out2, decoder_1_out3, decoder_2_out0, decoder_2_out1,
       decoder_2_out2, decoder_2_out3, decoder_2_out4, decoder_2_out5, decoder_2_out6, decoder_2_out7,
       decoder_3_out0, decoder_3_out1, decoder_3_out2, decoder_3_out3, decoder_3_out4, decoder_3_out5,
       decoder_3_out6, decoder_3_out7, decoder_4_out0, decoder_4_out1, decoder_4_out2, decoder_4_out3,
       decoder_4_out4, decoder_4_out5, decoder_4_out6, decoder_4_out7, decoder_5_out0, decoder_5_out1,
       decoder_5_out2, decoder_5_out3, decoder_5_out4, decoder_5_out5, decoder_5_out6, decoder_5_out7;
  wire [31:0] _00, _01, _02, _03, _04, _05, _06, _07, _08, _09, _10, _11, _12, _13, _14, _15, _16, _17, _18,
       _19, _20, _21, _22, _23, _24, _25, _26, _27, _28, _29, _30, _31;

  Register #(.width(32)) register_1 (.D(in_2), .en(in_10), .Q(HI_Out), .clk(in_7), .clr(in_8));
  Register #(.width(32)) register_2 (.D(in_5), .en(in_10), .Q(LO_Out), .clk(in_7), .clr(in_8));
  Decoder #(.select(2)) decoder_1 (
    .out0(decoder_1_out0), .out1(decoder_1_out1), .out2(decoder_1_out2), .out3(decoder_1_out3),
    .sel(in_4[4:3]), .en(in_6));
  Decoder #(.select(3), .disabled(0)) decoder_2 (
    .out0(decoder_2_out0), .out1(decoder_2_out1), .out2(decoder_2_out2), .out3(decoder_2_out3),
    .out4(decoder_2_out4), .out5(decoder_2_out5), .out6(decoder_2_out6), .out7(decoder_2_out7),
    .sel(in_4[2:0]), .en(decoder_1_out0));
  Decoder #(.select(3), .disabled(0)) decoder_3 (
    .out0(decoder_3_out0), .out1(decoder_3_out1), .out2(decoder_3_out2), .out3(decoder_3_out3),
    .out4(decoder_3_out4), .out5(decoder_3_out5), .out6(decoder_3_out6), .out7(decoder_3_out7),
    .sel(in_4[2:0]), .en(decoder_1_out1));
  Decoder #(.select(3), .disabled(0)) decoder_4 (
    .out0(decoder_4_out0), .out1(decoder_4_out1), .out2(decoder_4_out2), .out3(decoder_4_out3),
    .out4(decoder_4_out4), .out5(decoder_4_out5), .out6(decoder_4_out6), .out7(decoder_4_out7),
    .sel(in_4[2:0]), .en(decoder_1_out2));
  Decoder #(.select(3), .disabled(0)) decoder_5 (
    .out0(decoder_5_out0), .out1(decoder_5_out1), .out2(decoder_5_out2), .out3(decoder_5_out3),
    .out4(decoder_5_out4), .out5(decoder_5_out5), .out6(decoder_5_out6), .out7(decoder_5_out7),
    .sel(in_4[2:0]), .en(decoder_1_out3));
  Register #(.width(32)) u__00 (.D(in_9), .en(decoder_2_out0), .Q(_00), .clr(in_8));  // open: clk
  Register #(.width(32)) u__08 (.D(in_9), .en(decoder_3_out0), .Q(_08), .clk(in_7), .clr(in_8));
  Register #(.width(32)) u__16 (.D(in_9), .en(decoder_4_out0), .Q(_16), .clk(in_7), .clr(in_8));
  Register #(.width(32)) u__24 (.D(in_9), .en(decoder_5_out0), .Q(_24), .clk(in_7), .clr(in_8));
  Register #(.width(32)) u__01 (.D(in_9), .en(decoder_2_out1), .Q(_01), .clk(in_7), .clr(in_8));
  Register #(.width(32)) u__09 (.D(in_9), .en(decoder_3_out1), .Q(_09), .clk(in_7), .clr(in_8));
  Register #(.width(32)) u__17 (.D(in_9), .en(decoder_4_out1), .Q(_17), .clk(in_7), .clr(in_8));
  Register #(.width(32)) u__25 (.D(in_9), .en(decoder_5_out1), .Q(_25), .clk(in_7), .clr(in_8));
  Register #(.width(32)) u__02 (.D(in_9), .en(decoder_2_out2), .Q(_02), .clk(in_7), .clr(in_8));
  Register #(.width(32)) u__10 (.D(in_9), .en(decoder_3_out2), .Q(_10), .clk(in_7), .clr(in_8));
  Register #(.width(32)) u__18 (.D(in_9), .en(decoder_4_out2), .Q(_18), .clk(in_7), .clr(in_8));
  Register #(.width(32)) u__26 (.D(in_9), .en(decoder_5_out2), .Q(_26), .clk(in_7), .clr(in_8));
  Register #(.width(32)) u__03 (.D(in_9), .en(decoder_2_out3), .Q(_03), .clk(in_7), .clr(in_8));
  Register #(.width(32)) u__11 (.D(in_9), .en(decoder_3_out3), .Q(_11), .clk(in_7), .clr(in_8));
  Register #(.width(32)) u__19 (.D(in_9), .en(decoder_4_out3), .Q(_19), .clk(in_7), .clr(in_8));
  Register #(.width(32)) u__27 (.D(in_9), .en(decoder_5_out3), .Q(_27), .clk(in_7), .clr(in_8));
  Register #(.width(32)) u__04 (.D(in_9), .en(decoder_2_out4), .Q(_04), .clk(in_7), .clr(in_8));
  Register #(.width(32)) u__12 (.D(in_9), .en(decoder_3_out4), .Q(_12), .clk(in_7), .clr(in_8));
  Register #(.width(32)) u__20 (.D(in_9), .en(decoder_4_out4), .Q(_20), .clk(in_7), .clr(in_8));
  Register #(.width(32)) u__28 (.D(in_9), .en(decoder_5_out4), .Q(_28), .clk(in_7), .clr(in_8));
  Register #(.width(32)) u__05 (.D(in_9), .en(decoder_2_out5), .Q(_05), .clk(in_7), .clr(in_8));
  Register #(.width(32)) u__13 (.D(in_9), .en(decoder_3_out5), .Q(_13), .clk(in_7), .clr(in_8));
  Register #(.width(32)) u__21 (.D(in_9), .en(decoder_4_out5), .Q(_21), .clk(in_7), .clr(in_8));
  Register #(.width(32)) u__29 (.D(in_9), .en(decoder_5_out5), .Q(_29), .clk(in_7), .clr(in_8));
  Register #(.width(32)) u__06 (.D(in_9), .en(decoder_2_out6), .Q(_06), .clk(in_7), .clr(in_8));
  Register #(.width(32)) u__14 (.D(in_9), .en(decoder_3_out6), .Q(_14), .clk(in_7), .clr(in_8));
  Register #(.width(32)) u__22 (.D(in_9), .en(decoder_4_out6), .Q(_22), .clk(in_7), .clr(in_8));
  Register #(.width(32)) u__30 (.D(in_9), .en(decoder_5_out6), .Q(_30), .clk(in_7), .clr(in_8));
  Register #(.width(32)) u__07 (.D(in_9), .en(decoder_2_out7), .Q(_07), .clk(in_7), .clr(in_8));
  Register #(.width(32)) u__15 (.D(in_9), .en(decoder_3_out7), .Q(_15), .clk(in_7), .clr(in_8));
  Register #(.width(32)) u__23 (.D(in_9), .en(decoder_4_out7), .Q(_23), .clk(in_7), .clr(in_8));
  Register #(.width(32)) u__31 (.D(in_9), .en(decoder_5_out7), .Q(_31), .clk(in_7), .clr(in_8));
  Multiplexer #(.select(5), .width(32)) multiplexer_1 (
    .in0(_00), .in1(_01), .in2(_02), .in3(_03), .in4(_04), .in5(_05), .in6(_06), .in7(_07), .in8(_08),
    .in9(_09), .in10(_10), .in11(_11), .in12(_12), .in13(_13), .in14(_14), .in15(_15), .in16(_16),
    .in17(_17), .in18(_18), .in19(_19), .in20(_20), .in21(_21), .in22(_22), .in23(_23), .in24(_24),
    .in25(_25), .in26(_26), .in27(_27), .in28(_28), .in29(_29), .in30(_30), .in31(_31), .out(R1), .sel(in_1));  // open: en
  Multiplexer #(.select(5), .width(32)) multiplexer_2 (
    .in0(_00), .in1(_01), .in2(_02), .in3(_03), .in4(_04), .in5(_05), .in6(_06), .in7(_07), .in8(_08),
    .in9(_09), .in10(_10), .in11(_11), .in12(_12), .in13(_13), .in14(_14), .in15(_15), .in16(_16),
    .in17(_17), .in18(_18), .in19(_19), .in20(_20), .in21(_21), .in22(_22), .in23(_23), .in24(_24),
    .in25(_25), .in26(_26), .in27(_27), .in28(_28), .in29(_29), .in30(_30), .in31(_31), .out(R2), .sel(in_3));  // open: en

  // Other names for the same wires on the sheet: CLK = in_7; Dest_Address[4:0] = in_4; HI__in[31:0] = in_2;
  //   IN_Reg_1[4:0] = in_1; IN_Reg_2[4:0] = in_3; Input_Data[31:0] = in_9; LO__in[31:0] = in_5; Out_Reg_1[31:0] = R1;
  //   Out_Reg_2[31:0] = R2; Reset = in_8; WH___L = in_10; Write_Enable = in_6

  // Notes on the sheet:
  //   HI
  //   INPUTS
  //   OUTPUTS
  //   LO
endmodule

module Data_Path (
  input  [4:0] Rs,
  input  ALU_A_Selector,
  input  [31:0] Memory_Input,
  input  [4:0] Rt,
  input  [1:0] ALU_B_Selector,
  input  [4:0] Rd,
  input  [6:0] KBD_Data,
  input  Save_ALU_Result,
  input  RW,
  input  nRt_Rd,
  input  ALU_Sum,
  input  Reset,
  input  [5:0] Op_Code,
  input  Clock,
  input  [5:0] Func_Code,
  input  Write_Reg_File,
  input  Access_SP,
  input  [31:0] Offset,
  input  [31:0] Program_Counter,
  input  [2:0] DI_Selector,
  input  [31:0] Offset_x4,
  input  Write_SP,
  input  Compare_to_Zero,
  output out_24,
  output [31:0] RF_A,
  output [31:0] ALU_out,
  output [31:0] RF_B,
  output [31:0] ALU_Result
);

  wire alu_decoder_1_write_hi___lo, and_1_out, or_1_out, WH_L;
  wire [3:0] undriven;
  wire [4:0] multiplexer_2_out, multiplexer_3_out, multiplexer_4_out, multiplexer_4_out_2;
  wire [31:0] bit_extender_1_out, Hi, HI__in, Lo, multiplexer_1_out, multiplexer_5_out, multiplexer_6_out,
       multiplexer_7_out;

  assign bit_extender_1_out = {{25{1'b0}}, KBD_Data};  // Bit_Extender bit_extender_1
  Multiplexer #(.select(3), .width(32), .enable("false")) multiplexer_1 (
    .in0(ALU_out), .in1(ALU_Result), .in2(Hi), .in3(Lo), .in4(Memory_Input), .in5(bit_extender_1_out),
    .in6({32{1'b1}}), .out(multiplexer_1_out), .sel(DI_Selector));  // open: in7
  and and_1 (and_1_out, RW, ~WH_L, Write_Reg_File);  // AND_Gate
  Multiplexer #(.width(5), .enable("false")) multiplexer_2 (.in0(Rd), .in1(Rt), .out(multiplexer_2_out), .sel(nRt_Rd));
  Multiplexer #(.width(5), .enable("false")) multiplexer_3 (
    .in0({5{1'b1}}), .in1(multiplexer_2_out), .out(multiplexer_3_out), .sel(Write_SP));
  or or_1 (or_1_out, and_1_out, Write_SP);
  Register_File register_file_1 (
    .in_1(multiplexer_4_out_2), .in_3(multiplexer_4_out), .in_4(multiplexer_3_out), .in_6(or_1_out),
    .in_7(Clock), .in_8(Reset), .in_10(WH_L), .R1(RF_A), .R2(RF_B), .in_2(HI__in), .in_5(ALU_out),
    .in_9(multiplexer_1_out), .HI_Out(Hi), .LO_Out(Lo));
  Multiplexer #(.width(10), .enable("false")) multiplexer_4 (
    .in0({Rs, Rt}), .in1({{5{1'b1}}, Rs}), .out({multiplexer_4_out_2, multiplexer_4_out}), .sel(Access_SP));
  Multiplexer #(.width(32), .enable("false")) multiplexer_5 (
    .in0(Program_Counter), .in1(RF_A), .out(multiplexer_5_out), .sel(ALU_A_Selector));
  Multiplexer #(.width(32), .enable("false")) multiplexer_6 (
    .in0(RF_B), .in1({32{1'b0}}), .out(multiplexer_6_out), .sel(Compare_to_Zero));
  Multiplexer #(.select(2), .width(32), .enable("false")) multiplexer_7 (
    .in0(multiplexer_6_out), .in1(32'h4), .in2(Offset), .in3(Offset_x4), .out(multiplexer_7_out),
    .sel(ALU_B_Selector));
  ALU alu_1 (
    .in_1(undriven), .Equal(out_24), .in_2(multiplexer_5_out), .in_3(multiplexer_7_out), .out_6(ALU_out),
    .out_7(HI__in));  // open: Carry_Flag, Overflow, Zero_Flag
  ALU_Decoder alu_decoder_1 (
    .Op_Code(Op_Code), .Func_Code(Func_Code), .Sum(ALU_Sum), .ALU_Operation(undriven),
    .Write_Hi___Lo(alu_decoder_1_write_hi___lo));
  and and_2 (WH_L, Write_Reg_File, alu_decoder_1_write_hi___lo);
  Register #(.width(32)) register_1 (.en(Save_ALU_Result), .Q(ALU_Result), .clk(Clock), .clr(Reset));  // open: D

  // Other names for the same wires on the sheet: A[31:0] = RF_A; A_Sel = ALU_A_Selector; Acc_SP = Access_SP;
  //   B[31:0] = RF_B; B_Sel[1:0] = ALU_B_Selector; CLK = Clock; DI_Sel[2:0] = DI_Selector; Equal = out_24;
  //   FC[5:0] = Func_Code; LO__in[31:0] = ALU_out; Mem_In[31:0] = Memory_Input; OC[5:0] = Op_Code; Os[31:0] = Offset;
  //   Os_x4[31:0] = Offset_x4; PC[31:0] = Program_Counter; RST = Reset; Save_ALU = Save_ALU_Result; tunnel = ALU_Sum;
  //   WRF = Write_Reg_File; WSP = Write_SP; Zero = Compare_to_Zero

  // Notes on the sheet:
  //   Branch Control
  //   INPUTS
  //   OUTPUTS
endmodule

module ALU (
  input  [3:0] in_1,
  input  [31:0] in_2,
  input  [31:0] in_3,
  output Carry_Flag,
  output Overflow,
  output [31:0] out_6,
  output [31:0] out_7,
  output Equal,
  output Zero_Flag
);

  wire Clk, comparator_1_lt, comparator_2_gt;
  wire [1:0] adder_with_overflow_detection_1_overflow, substractor_with_overflow_detection_1_out_6;
  wire [31:0] adder_with_overflow_detection_1_out_5, and_1_out, bit_extender_1_out, bit_extender_2_out,
       divider_1_out, divider_1_rem, divider_2_out, divider_2_rem, multiplier_1_cout, multiplier_1_out,
       multiplier_2_cout, multiplier_2_out, nor_1_out, or_1_out, random_1_out, shifter_1_out, shifter_2_out,
       shifter_3_out, substractor_with_overflow_detection_1_out_5, xor_1_out;

  // Probe on in_2
  // Probe on in_3
  Adder_with_overflow_detection adder_with_overflow_detection_1 (
    .Carry_Flag(adder_with_overflow_detection_1_overflow[1]), .in_2(in_2), .in_3(in_3),
    .out_5(adder_with_overflow_detection_1_out_5), .Overflow(adder_with_overflow_detection_1_overflow[0]));  // open: Carry_in
  Substractor_with_overflow_detection substractor_with_overflow_detection_1 (
    .out_4(substractor_with_overflow_detection_1_out_6[1]), .in_1(in_2), .in_2(in_3),
    .out_5(substractor_with_overflow_detection_1_out_5),
    .out_6(substractor_with_overflow_detection_1_out_6[0]));  // open: in_3
  Clock clock_1 (.out(Clk));
  Shifter #(.width(32)) shifter_1 (.in(in_2), .\dist (in_3[4:0]), .out(shifter_1_out));
  Shifter #(.width(32), .shift("lr")) shifter_2 (.in(in_2), .\dist (in_3[4:0]), .out(shifter_2_out));
  assign and_1_out = in_2 & in_3;  // AND_Gate and_1, 32 bits wide
  Shifter #(.width(32), .shift("ar")) shifter_3 (.in(in_2), .\dist (in_3[4:0]), .out(shifter_3_out));
  assign or_1_out = in_2 | in_3;  // OR_Gate or_1, 32 bits wide
  assign nor_1_out = ~(in_2 | in_3);  // NOR_Gate nor_1, 32 bits wide
  assign xor_1_out = in_2 ^ in_3;  // XOR_Gate xor_1, 32 bits wide
  Comparator #(.width(32)) comparator_1 (.a(in_2), .b(in_3), .lt(comparator_1_lt));  // open: gt, eq
  Random #(.width(32)) random_1 (.clk(Clk), .next(1'b1), .out(random_1_out));  // open: clr
  Comparator #(.width(32)) comparator_2 (.a(in_2), .b(in_3), .gt(comparator_2_gt), .eq(Equal));  // open: lt
  Multiplier #(.width(32)) multiplier_1 (
    .a(in_2), .b(in_3), .out(multiplier_1_out), .cout(multiplier_1_cout));  // open: cin
  Divider #(.width(32)) divider_1 (.a(in_2), .b(in_3), .out(divider_1_out), .rem(divider_1_rem));  // open: upper
  Multiplier #(.width(32)) multiplier_2 (
    .a(in_2), .b(in_3), .out(multiplier_2_out), .cout(multiplier_2_cout));  // open: cin
  Divider #(.width(32)) divider_2 (.a(in_2), .b(in_3), .out(divider_2_out), .rem(divider_2_rem));  // open: upper
  // Probe on in_1
  assign bit_extender_1_out = {{31{1'b0}}, comparator_1_lt};  // Bit_Extender bit_extender_1
  assign bit_extender_2_out = {{31{1'b0}}, comparator_2_gt};  // Bit_Extender bit_extender_2
  Multiplexer #(.select(4), .width(2)) multiplexer_1 (
    .in0(adder_with_overflow_detection_1_overflow), .in1(substractor_with_overflow_detection_1_out_6),
    .in2(2'b00), .in3(2'b00), .in4(2'b00), .in5(2'b00), .in6(2'b00), .in7(2'b00), .in8(2'b00), .in9(2'b00),
    .in10(2'b00), .in11(2'b00), .in12(2'b00), .in13(2'b00), .in14(2'b00), .in15(2'b00),
    .out({Overflow, Carry_Flag}), .sel(in_1));  // open: en
  // Probe on out_6
  Multiplexer #(.select(4), .width(32)) multiplexer_2 (
    .in0(adder_with_overflow_detection_1_out_5), .in1(substractor_with_overflow_detection_1_out_5),
    .in2(shifter_1_out), .in3(shifter_2_out), .in4(and_1_out), .in5(shifter_3_out), .in6(or_1_out),
    .in7(nor_1_out), .in8(xor_1_out), .in9(bit_extender_1_out), .in10(random_1_out),
    .in11(bit_extender_2_out), .in12(multiplier_1_out), .in13(divider_1_out), .in14(multiplier_2_out),
    .in15(divider_2_out), .out(out_6), .sel(in_1));  // open: en
  Multiplexer #(.select(4), .width(32)) multiplexer_3 (
    .in0({32{1'b0}}), .in1({32{1'b0}}), .in2({32{1'b0}}), .in3({32{1'b0}}), .in4({32{1'b0}}),
    .in5({32{1'b0}}), .in6({32{1'b0}}), .in7({32{1'b0}}), .in8({32{1'b0}}), .in9({32{1'b0}}),
    .in10({32{1'b0}}), .in11({32{1'b0}}), .in12(multiplier_1_cout), .in13(divider_1_rem),
    .in14(multiplier_2_cout), .in15(divider_2_rem), .out(out_7), .sel(in_1));  // open: en
  // Probe on out_7
  Comparator #(.width(32)) comparator_3 (.a({32{1'b0}}), .b(out_6), .eq(Zero_Flag));  // open: gt, lt

  // Other names for the same wires on the sheet: CF = Carry_Flag; OF = Overflow; A[31:0] = in_2; B[31:0] = in_3;
  //   Help_Result[31:0] = out_7; Main_Result[31:0] = out_6; OP[3:0] = in_1; Zero = Zero_Flag

  // Notes on the sheet:
  //   Inputs
  //   and
  //   arithmetic right
  //   or
  //   nor
  //   xor
  //   Adder with OF
  //   substractor with OF
  //   logical left
  //   logical right
  //   less than
  //   Random generator
  //   greater than
  //   signed mult
  //   signed div
  //   unsigned mult
  //   unsigned div
  //   Outputs
endmodule

module ALU_Decoder (
  input  [3:0] ALU_Operation,
  input  [5:0] Op_Code,
  input  [5:0] Func_Code,
  input  Sum,
  output Write_Hi___Lo
);

  wire and_5_out;
  wire [1:0] nor_1_out;
  wire [2:2] or_1_out;
  wire [3:0] and_3_out, multiplexer_1_out, multiplexer_2_out;

  and and_1 (and_3_out[3], Op_Code[3], Op_Code[1]);
  and and_2 (and_3_out[2], Op_Code[2], ~Op_Code[1]);  // AND_Gate
  and and_3 (and_3_out[0], Op_Code[3], ~Op_Code[2], Op_Code[1]);  // AND_Gate
  or or_1 (or_1_out[2], Func_Code[1], Func_Code[4]);
  Multiplexer #(.width(4), .enable("false")) multiplexer_1 (
    .in0(4'b1001), .in1({and_3_out[3:2], Op_Code[0], and_3_out[0]}), .out(multiplexer_1_out), .sel(Op_Code[3]));
  and and_4 (nor_1_out[1], Op_Code[5], Op_Code[4], Op_Code[3], ~Op_Code[2], ~Op_Code[1], ~Op_Code[0]);  // AND_Gate
  and and_5 (and_5_out, Func_Code[3], Func_Code[4], ~Func_Code[5]);  // AND_Gate
  Multiplexer #(.select(2), .width(4), .enable("false")) multiplexer_2 (
    .in0(multiplexer_1_out), .in1({Func_Code[3], or_1_out[2], Func_Code[0], Func_Code[2]}),
    .in2(Func_Code[3:0]), .in3(Func_Code[3:0]), .out(multiplexer_2_out), .sel(nor_1_out));
  Multiplexer #(.width(4), .enable("false")) multiplexer_3 (
    .in0(multiplexer_2_out), .in1(4'b0000), .out(ALU_Operation), .sel(Sum));
  nor nor_1 (nor_1_out[0], Op_Code[5], Op_Code[4], Op_Code[3], Op_Code[2], Op_Code[1], Op_Code[0], 1'b0);
  and and_6 (Write_Hi___Lo, nor_1_out[0], and_5_out);

  // Notes on the sheet:
  //   add
  //   sub
  //   logical left
  //   logical right
  //   or
  //   nor
  //   xor
  //   divu
  //   Operation
  //   pop
  //   push
  //   Operation
  //   and
  //   arithmetic right
  //   slt
  //   rnd (Op 11 1111)
  //   sltu
  //   mult
  //   div
  //   mulu
  //   Op-Code: 11 1000
  //   OP-Code: 00 0000
  //   Func code
  //   10 0000
  //   10 0001
  //   10 0010
  //   10 0011
  //   10 0100
  //   10 0101
  //   10 0110
  //   10 0111
  //   10 1000
  //   10 1001
  //   10 1010
  //   10 1011
  //   10 1100
  //   10 1101
  //   10 1110
  //   10 1111
  //   ALU Op
  //   0000
  //   0001
  //   ALU Op
  //   0000
  //   0001
  //   0010
  //   0011
  //   0100
  //   0101
  //   0110
  //   0111
  //   1000
  //   1001
  //   1010
  //   1011
  //   1100
  //   1101
  //   1110
  //   1111
  //   ALU Op: 1001
  //   Operation
  //   beq
  //   bne
  //   blez
  //   bgtz
  //   bltz
  //   Operation
  //   addi
  //   andi
  //   ori
  //   xori
  //   slti
  //   sltiu
  //   Op code
  //   00 0100
  //   00 0101
  //   00 0110
  //   00 0111
  //   00 0001
  //   Op code
  //   00 1000
  //   00 1100
  //   00 1101
  //   00 1110
  //   00 1010
  //   00 1011
  //   ALU Op
  //   0000
  //   0100
  //   0110
  //   1000
  //   1001
  //   1011
endmodule

module Adder_with_overflow_detection (
  input  Carry_in,
  input  [31:0] in_2,
  input  [31:0] in_3,
  output Carry_Flag,
  output [31:0] out_5,
  output Overflow
);

  wire adder_1_cout;

  // Probe on in_2
  Adder #(.width(31)) adder_1 (.a(in_2[30:0]), .b(in_3[30:0]), .out(out_5[30:0]), .cin(Carry_in), .cout(adder_1_cout));
  Adder #(.width(1)) adder_2 (.a(in_2[31]), .b(in_3[31]), .out(out_5[31]), .cin(adder_1_cout), .cout(Carry_Flag));
  // Probe on in_3
  xor xor_1 (Overflow, adder_1_cout, Carry_Flag);
  // Probe on out_5

  // Other names for the same wires on the sheet: A[31:0] = in_2; B[31:0] = in_3; c_in = Carry_in; CF = Carry_Flag;
  //   OF = Overflow; Result[31:0] = out_5

  // Notes on the sheet:
  //   Inputs
  //   Outputs
endmodule

module Substractor_with_overflow_detection (
  input  [31:0] in_1,
  input  [31:0] in_2,
  input  in_3,
  output out_4,
  output [31:0] out_5,
  output out_6
);

  wire subtractor_1_bout;

  // Probe on in_1
  Subtractor #(.width(31)) subtractor_1 (
    .a(in_1[30:0]), .b(in_2[30:0]), .out(out_5[30:0]), .bin(in_3), .bout(subtractor_1_bout));
  Subtractor #(.width(1)) subtractor_2 (
    .a(in_1[31]), .b(in_2[31]), .out(out_5[31]), .bin(subtractor_1_bout), .bout(out_4));
  // Probe on in_2
  xor xor_1 (out_6, subtractor_1_bout, out_4);
  // Probe on out_5

  // Other names for the same wires on the sheet: A[31:0] = in_1; B[31:0] = in_2; b_in = in_3; CF = out_4; OF = out_6;
  //   Result[31:0] = out_5

  // Notes on the sheet:
  //   Inputs
  //   Outputs
endmodule

module Instruction_decoder (
  input  [31:0] Instruction,
  input  Write_Instruction,
  input  Clock,
  input  Reset,
  input  [31:0] Program_Counter__updated,
  output Write_Rd,
  output jmp,
  output [15:0] Offset,
  output nRead_Write,
  output [5:0] Op_Code,
  output [1:0] Jump_Value_Selector,
  output [4:0] Rs,
  output [5:0] Func_Code,
  output [4:0] Rd,
  output [4:0] Rt,
  output [31:0] Jump_Value,
  output Inmediate,
  output nHi_Lo,
  output [2:0] Operation_Type,
  output nPush_Pop,
  output nRead_Write_Memory,
  output [2:0] Jump_Type
);

  wire and_3_out, and_4_out, and_5_out, and_6_out, and_7_out, and_10_out, demultiplexer_1_out0,
       demultiplexer_1_out1, Halt, IO, J_Type, jmp_t, Memory_Op, Move_Hi_Lo, NOP, nor_1_out, nor_3_out,
       nor_5_out, nor_7_out, nor_8_out, nor_9_out, or_2_out, or_4_out, or_5_out, Stack;

  and and_1 (Move_Hi_Lo, Write_Rd, ~Func_Code[3], Func_Code[4], ~Func_Code[5]);  // AND_Gate
  and and_2 (Memory_Op, Op_Code[5], Op_Code[5], ~Op_Code[5], Op_Code[5]);  // AND_Gate
  Register #(.width(32)) register_1 (
    .D(Instruction), .en(Write_Instruction), .Q({{16{Op_Code[5]}}, Offset[15:6], Func_Code}), .clk(Clock),
    .clr(Reset));
  nor nor_1 (nor_1_out, Op_Code[5], Op_Code[5]);
  nor nor_2 (Inmediate, ~Op_Code[5], Op_Code[5], Op_Code[5]);  // NOR_Gate
  not not_1 (nHi_Lo, Func_Code[1]);
  not not_2 (nPush_Pop, Op_Code[5]);
  Multiplexer #(.enable("false")) multiplexer_1 (
    .in0(Op_Code[5]), .in1(Func_Code[0]), .out(nRead_Write_Memory), .sel(Write_Rd));
  or or_1 (nRead_Write, Write_Rd, nor_1_out);
  or or_2 (or_2_out, Inmediate, nor_3_out);
  nor nor_3 (nor_3_out, Move_Hi_Lo, NOP);
  Demultiplexer #(.enable("false")) demultiplexer_1 (
    .out0(demultiplexer_1_out0), .out1(demultiplexer_1_out1), .in(IO), .sel(Func_Code[2]));
  nor nor_4 (NOP, Func_Code[0], Func_Code[1], Func_Code[2], Func_Code[3], Func_Code[4], Func_Code[5], Offset[6], Offset[7], Offset[8], Offset[9], Offset[10], Offset[11], Offset[12], Offset[13], Offset[14], Offset[15], Op_Code[5], Op_Code[5], Op_Code[5], Op_Code[5], Op_Code[5], Op_Code[5], Op_Code[5], Op_Code[5], Op_Code[5], Op_Code[5], Op_Code[5], Op_Code[5], Op_Code[5], Op_Code[5], Op_Code[5], Op_Code[5]);
  Priority_Encoder priority_encoder_1 (
    .in0(or_2_out), .in1(jmp_t), .in2(Memory_Op), .in3(Move_Hi_Lo), .in4(Stack), .in5(demultiplexer_1_out0),
    .in6(demultiplexer_1_out1), .in7(Halt), .out(Operation_Type));  // open: en_in, gs, en_out
  and and_3 (and_3_out, Op_Code[5], Op_Code[5]);
  nor nor_5 (nor_5_out, Op_Code[5], Op_Code[5], Op_Code[5], Op_Code[5], Op_Code[5], Op_Code[5]);
  nor nor_6 (J_Type, Op_Code[5], Op_Code[5], Op_Code[5], Op_Code[5], Op_Code[5], Op_Code[5]);
  or or_3 (Write_Rd, and_3_out, nor_5_out);
  and and_4 (and_4_out, ~Op_Code[5], Op_Code[5], ~Op_Code[5]);  // AND_Gate
  or or_4 (or_4_out, Op_Code[5], Op_Code[5], Op_Code[5]);
  nor nor_7 (nor_7_out, Op_Code[5], Op_Code[5], Op_Code[5]);
  nor nor_8 (nor_8_out, Op_Code[5], Op_Code[5], Op_Code[5]);
  and and_5 (and_5_out, Op_Code[5], Op_Code[5], Op_Code[5]);
  and and_6 (and_6_out, Op_Code[5], Op_Code[5], Op_Code[5]);
  and and_7 (and_7_out, Func_Code[0], Func_Code[1], Func_Code[3], Func_Code[4], Func_Code[5]);
  or or_5 (or_5_out, Func_Code[2], Func_Code[0]);
  and and_8 (Jump_Value_Selector[0], and_4_out, or_4_out, nor_7_out);
  and and_9 (Stack, nor_8_out, and_6_out);
  and and_10 (and_10_out, and_5_out, and_6_out);
  and and_11 (Halt, and_10_out, and_7_out);
  and and_12 (IO, and_10_out, or_5_out);
  or or_6 (jmp, J_Type, Jump_Value_Selector[1], Jump_Value_Selector[0]);
  Multiplexer #(.width(3), .enable("false")) multiplexer_2 (
    .in0({3{Op_Code[5]}}), .in1(3'b000), .out(Jump_Type), .sel(J_Type));
  or or_7 (jmp_t, NOP, jmp);
  Multiplexer #(.width(32), .enable("false")) multiplexer_3 (
    .in0(Program_Counter__updated),
    .in1({Program_Counter__updated[31:28], {10{Op_Code[5]}}, Offset[15:6], Func_Code, 2'b00}),
    .out(Jump_Value), .sel(J_Type));
  and and_13 (Jump_Value_Selector[1], nor_5_out, nor_9_out);
  nor nor_9 (nor_9_out, Func_Code[0], Func_Code[1], Func_Code[2], ~Func_Code[3], Func_Code[4], Func_Code[5]);  // NOR_Gate

  assign Offset[5:0] = Func_Code;
  assign Op_Code[4:0] = {5{Op_Code[5]}};
  assign Rd = Offset[15:11];
  assign Rs = {5{Op_Code[5]}};
  assign Rt = {5{Op_Code[5]}};

  // Other names for the same wires on the sheet: Instruction_t[31:0] = {{16{Op_Code[5]}}, Offset[15:6], Func_Code};
  //   PC[31:0] = Program_Counter__updated; Branch = Jump_Value_Selector[0]; JR = Jump_Value_Selector[1];
  //   R_Type = Write_Rd

  // Notes on the sheet:
  //   Inputs
  //   Register File
  //   En el register file paso como selector del registro a escribir un multiplexer
  //   con con Rt y Rd de entradas y este bit (R-Type) como selector
  //   Control Unit
  //   MISC
  //   Common
  //   OUTPUTS
  //   Branch Control
  //   En el branch control se pasa el jump value, el offsett trabajado y
  //   el contenido de Rs por un multiplexer con este selector
  //   Si es nop se mantiene el PC, si no se construye la nueva direccion
  //   Selector que usara el branch control
  //   para determinar el tipo de salto
endmodule

module Branch_Control (
  input  Jump_Operation,
  input  [31:0] Jump_Value,
  input  [2:0] Jump_Selector,
  input  [31:0] Next_Program_Counter_Value,
  input  Clock,
  input  ALU_Less,
  input  Try_Jump,
  input  ALU_Equals,
  input  Update_PC,
  input  Reset,
  output [31:0] Program_Counter,
  output out_12
);

  wire and_1_out, and_2_out, and_3_out, multiplexer_2_out, not_1_out, not_2_out, or_1_out, or_2_out;
  wire [31:0] multiplexer_1_out;

  Multiplexer #(.width(32), .enable("false")) multiplexer_1 (
    .in0(Next_Program_Counter_Value), .in1(Jump_Value), .out(multiplexer_1_out), .sel(and_2_out));
  and and_1 (and_1_out, and_2_out, Try_Jump);
  and and_2 (and_2_out, Jump_Operation, multiplexer_2_out);
  Multiplexer #(.select(3), .enable("false")) multiplexer_2 (
    .in0(1'b1), .in1(ALU_Less), .in2(1'b1), .in3(1'b0), .in4(ALU_Equals), .in5(not_1_out), .in6(or_2_out),
    .in7(not_2_out), .out(multiplexer_2_out), .sel(Jump_Selector));
  Register #(.width(32)) PC (.D(multiplexer_1_out), .en(or_1_out), .Q(Program_Counter), .clk(Clock), .clr(Reset));
  or or_1 (or_1_out, and_1_out, Update_PC);
  not not_1 (not_1_out, ALU_Equals);
  not not_2 (not_2_out, or_2_out);
  and and_3 (and_3_out, ~Jump_Selector[1], Jump_Selector[2]);  // AND_Gate
  or or_2 (or_2_out, ALU_Less, ALU_Equals);
  and and_4 (out_12, and_3_out, Jump_Operation);

  // Other names for the same wires on the sheet: CLK = Clock; Equals = ALU_Equals; Imp = Jump_Operation;
  //   Jump_S[2:0] = Jump_Selector; Jump_V[31:0] = Jump_Value; Less = ALU_Less; PC[31:0] = Next_Program_Counter_Value;
  //   Update = Update_PC

  // Notes on the sheet:
  //   INPUTS
  //   OUTPUT
endmodule

module Access_Memory (
  input  [31:0] Target_Address,
  input  [31:0] Ram_O0,
  input  [31:0] Ram_O1,
  input  [31:0] To_Write,
  input  [31:0] Ram_O2,
  input  [31:0] Ram_O3,
  output [15:0] Address,
  output [3:0] Mask,
  output [31:0] Ram_I0,
  output [31:0] Ram_I1,
  output [31:0] Ram_out,
  output [31:0] Ram_I2,
  output [31:0] Ram_I3
);

  wire [31:0] divider_1_out;
  wire [31:16] divider_2_out;

  Multiplexer #(.select(2), .width(32), .enable("false")) multiplexer_1 (
    .in0(Ram_O0), .in1(Ram_O1), .in2(Ram_O2), .in3(Ram_O3),
    .out({Ram_out[7:0], Ram_out[15:8], Ram_out[23:16], Ram_out[31:24]}), .sel(divider_1_out[1:0]));
  Divider #(.width(32)) divider_1 (.a(Target_Address), .b(32'h4), .out(divider_1_out));  // open: upper, rem
  Decoder #(.select(2), .enable("false")) decoder_1 (
    .out0(Mask[0]), .out1(Mask[1]), .out2(Mask[2]), .out3(Mask[3]), .sel(divider_1_out[1:0]));
  Divider #(.width(32)) divider_2 (.a(divider_1_out), .b(32'h4), .out({divider_2_out, Address}));  // open: upper, rem

  assign Ram_I0 = {To_Write[7:0], To_Write[15:8], To_Write[23:16], To_Write[31:24]};
  assign Ram_I1 = {To_Write[7:0], To_Write[15:8], To_Write[23:16], To_Write[31:24]};
  assign Ram_I2 = {To_Write[7:0], To_Write[15:8], To_Write[23:16], To_Write[31:24]};
  assign Ram_I3 = {To_Write[7:0], To_Write[15:8], To_Write[23:16], To_Write[31:24]};
endmodule

module Chronometer (
  input  INPUTS,
  input  in_2,
  input  [3:0] in_3,
  input  in_4,
  output out_5,
  output out_6
);

  wire comparator_2_eq, d_ff_1_q, or_1_out;
  wire [4:0] counter_1_q;

  Clock clock_1 ();  // open: out
  Counter #(.width(5), .max('h1f)) counter_1 (
    .load(1'b0), .count(in_2), .Q(counter_1_q), .clk(INPUTS), .clr(or_1_out));  // open: D, carry
  Comparator #(.width(5)) comparator_1 (.a({1'b0, in_3}), .b(counter_1_q), .eq(out_6));  // open: gt, lt
  Comparator #(.width(5)) comparator_2 (.a(counter_1_q), .b({5{1'b0}}), .eq(comparator_2_eq));  // open: gt, lt
  or or_1 (or_1_out, d_ff_1_q, in_4);
  D_Flip_Flop #(.trigger("falling")) d_ff_1 (
    .clk(INPUTS), .D(out_6), .Q(d_ff_1_q), .reset(or_1_out));  // open: Qn, preset, en
  or or_2 (out_5, ~comparator_2_eq, in_2);  // OR_Gate

  // Other names for the same wires on the sheet: Frecuency[3:0] = in_3; Clock = INPUTS; Counting = out_5; END = out_6;
  //   Reset_Signal = in_4; Start_Signal = in_2

  // Notes on the sheet:
  //   OUTPUTS
endmodule
